// Logisim project 4BitComparator.circ as structural Verilog: 7 circuits, main circuit main
module main (
  input  A,
  input  A2,
  input  A1,
  input  A0,
  input  B,
  input  B2,
  input  B1,
  input  B0,
  input  C,
  output A_B,
  output A_B_2,
  output A_B_3
);

  wire n4bitsignedcomparator_1_a_b, n4bitsignedcomparator_1_a_b_2, n4bitsignedcomparator_1_a_b_3,
       n4bitunsignedcomparator_1_a_b, n4bitunsignedcomparator_1_a_b_2, n4bitunsignedcomparator_1_a_b_3;

  _4BitUnsignedComparator u_4bitunsignedcomparator_1 (
    .A3(A), .A2(A2), .A1(A1), .A0(A0), .B3(B), .B2(B2), .B1(B1), .B0(B0),
    .A_B(n4bitunsignedcomparator_1_a_b), .A_B_2(n4bitunsignedcomparator_1_a_b_2),
    .A_B_3(n4bitunsignedcomparator_1_a_b_3));
  Multi multi_1 (.in_2(n4bitsignedcomparator_1_a_b), .in_3(n4bitunsignedcomparator_1_a_b), .in_1(C), .out_4(A_B));
  Multi multi_2 (.in_2(n4bitsignedcomparator_1_a_b_2), .in_3(n4bitunsignedcomparator_1_a_b_2), .in_1(C), .out_4(A_B_2));
  _4BitSignedComparator u_4bitsignedcomparator_1 (
    .A3(A), .A2(A2), .A1(A1), .A0(A0), .B3(B), .B2(B2), .B1(B1), .B0(B0), .A_B(n4bitsignedcomparator_1_a_b),
    .A_B_2(n4bitsignedcomparator_1_a_b_2), .A_B_3(n4bitsignedcomparator_1_a_b_3));
  Multi multi_3 (.in_2(n4bitsignedcomparator_1_a_b_3), .in_3(n4bitunsignedcomparator_1_a_b_3), .in_1(C), .out_4(A_B_3));

  // Notes on the sheet:
  //   A3
  //   Unsigned
  //   Signed
  //   B3
endmodule

module _4BitEqualsUnsignedAndSigned (
  input  A,
  input  A2,
  input  A1,
  input  A0,
  input  B,
  input  B2,
  input  B1,
  input  B0,
  output A_B
);

  wire not_1_out, not_2_out, not_3_out, not_4_out, xor_1_out, xor_2_out, xor_3_out, xor_4_out;

  xor xor_1 (xor_1_out, A, B);
  not not_1 (not_1_out, xor_1_out);
  xor xor_2 (xor_2_out, A2, B2);
  not not_2 (not_2_out, xor_2_out);
  and and_1 (A_B, not_1_out, not_2_out, not_3_out, not_4_out);
  xor xor_3 (xor_3_out, A1, B1);
  not not_3 (not_3_out, xor_3_out);
  xor xor_4 (xor_4_out, A0, B0);
  not not_4 (not_4_out, xor_4_out);

  // Notes on the sheet:
  //   A3
  //   B3
endmodule

module _4BitGreaterUnsigned (
  input  A,
  input  A2,
  input  A1,
  input  A0,
  input  B,
  input  B2,
  input  B1,
  input  B0,
  output A_B
);

  wire and_1_out, and_2_out, and_3_out, and_4_out, not_1_out, not_2_out, not_3_out, not_4_out, not_5_out,
       not_6_out, not_7_out, not_8_out, not_9_out, not_10_out, xor_1_out, xor_2_out, xor_3_out, xor_4_out,
       xor_5_out, xor_6_out;

  and and_1 (and_1_out, A, not_10_out);
  xor xor_1 (xor_1_out, A, B);
  not not_1 (not_1_out, B2);
  not not_2 (not_2_out, xor_1_out);
  and and_2 (and_2_out, not_2_out, A2, not_1_out);
  or or_1 (A_B, and_1_out, and_2_out, and_3_out, and_4_out);
  xor xor_2 (xor_2_out, A, B);
  not not_3 (not_3_out, xor_2_out);
  and and_3 (and_3_out, not_3_out, not_4_out, A1, not_6_out);
  xor xor_3 (xor_3_out, A2, B2);
  not not_4 (not_4_out, xor_3_out);
  xor xor_4 (xor_4_out, A, B);
  not not_5 (not_5_out, xor_4_out);
  not not_6 (not_6_out, B1);
  xor xor_5 (xor_5_out, A2, B2);
  not not_7 (not_7_out, xor_5_out);
  and and_4 (and_4_out, not_5_out, not_7_out, not_8_out, A0, not_9_out);
  xor xor_6 (xor_6_out, A1, B1);
  not not_8 (not_8_out, xor_6_out);
  not not_9 (not_9_out, B0);
  not not_10 (not_10_out, B);

  // Notes on the sheet:
  //   A3
  //   B3
endmodule

module _4BitLessUnsigned (
  input  A,
  input  A2,
  input  A1,
  input  A0,
  input  B,
  input  B2,
  input  B1,
  input  B0,
  output A_B
);

  wire and_1_out, and_2_out, and_3_out, and_4_out, not_1_out, not_2_out, not_3_out, not_4_out, not_5_out,
       not_6_out, not_7_out, not_8_out, not_9_out, not_10_out, xor_1_out, xor_2_out, xor_3_out, xor_4_out,
       xor_5_out, xor_6_out;

  not not_1 (not_1_out, A);
  and and_1 (and_1_out, not_1_out, B);
  xor xor_1 (xor_1_out, A, B);
  not not_2 (not_2_out, xor_1_out);
  and and_2 (and_2_out, not_2_out, not_3_out, B2);
  not not_3 (not_3_out, A2);
  xor xor_2 (xor_2_out, A, B);
  not not_4 (not_4_out, xor_2_out);
  xor xor_3 (xor_3_out, A2, B2);
  not not_5 (not_5_out, xor_3_out);
  not not_6 (not_6_out, A1);
  and and_3 (and_3_out, not_4_out, not_5_out, not_6_out, B1);
  or or_1 (A_B, and_1_out, and_2_out, and_3_out, and_4_out);
  xor xor_4 (xor_4_out, A, B);
  not not_7 (not_7_out, xor_4_out);
  and and_4 (and_4_out, not_7_out, not_8_out, not_9_out, not_10_out, B0);
  xor xor_5 (xor_5_out, A2, B2);
  not not_8 (not_8_out, xor_5_out);
  xor xor_6 (xor_6_out, A1, B1);
  not not_9 (not_9_out, xor_6_out);
  not not_10 (not_10_out, A0);

  // Notes on the sheet:
  //   A3
  //   B3
endmodule

module _4BitUnsignedComparator (
  input  A3,
  input  A2,
  input  A1,
  input  A0,
  input  B3,
  input  B2,
  input  B1,
  input  B0,
  output A_B,
  output A_B_2,
  output A_B_3
);

  _4BitGreaterUnsigned u_4bitgreaterunsigned_1 (
    .A(A3), .A2(A2), .A1(A1), .A0(A0), .B(B3), .B2(B2), .B1(B1), .B0(B0), .A_B(A_B));
  _4BitEqualsUnsignedAndSigned u_4bitequalsunsignedandsigned_1 (
    .A(A3), .A2(A2), .A1(A1), .A0(A0), .B(B3), .B2(B2), .B1(B1), .B0(B0), .A_B(A_B_2));
  _4BitLessUnsigned u_4bitlessunsigned_1 (
    .A(A3), .A2(A2), .A1(A1), .A0(A0), .B(B3), .B2(B2), .B1(B1), .B0(B0), .A_B(A_B_3));
endmodule

module _4BitSignedComparator (
  input  A3,
  input  A2,
  input  A1,
  input  A0,
  input  B3,
  input  B2,
  input  B1,
  input  B0,
  output A_B,
  output A_B_2,
  output A_B_3
);

  wire not_1_out, not_2_out;

  not not_1 (not_1_out, A3);
  _4BitGreaterUnsigned u_4bitgreaterunsigned_1 (
    .A(not_1_out), .A2(A2), .A1(A1), .A0(A0), .B(not_2_out), .B2(B2), .B1(B1), .B0(B0), .A_B(A_B));
  _4BitEqualsUnsignedAndSigned u_4bitequalsunsignedandsigned_1 (
    .A(not_1_out), .A2(A2), .A1(A1), .A0(A0), .B(not_2_out), .B2(B2), .B1(B1), .B0(B0), .A_B(A_B_2));
  not not_2 (not_2_out, B3);
  _4BitLessUnsigned u_4bitlessunsigned_1 (
    .A(not_1_out), .A2(A2), .A1(A1), .A0(A0), .B(not_2_out), .B2(B2), .B1(B1), .B0(B0), .A_B(A_B_3));
endmodule

module Multi (
  input  in_1,
  input  in_2,
  input  in_3,
  output out_4
);

  wire and_1_out, and_2_out, not_1_out;

  not not_1 (not_1_out, in_1);
  and and_1 (and_1_out, in_2, in_1);
  and and_2 (and_2_out, in_3, not_1_out);
  xor xor_1 (out_4, and_1_out, and_2_out);
endmodule
